// Digital circuit ALU.dig as structural Verilog
module ALU (
  input  [3:0] Op,
  input  [31:0] A,
  input  [31:0] B,
  output [31:0] Out,
  output EQUAL,
  output LESS,
  output LESS_U
);

  wire SRA, SUB;
  wire [31:0] adder32_1_a_plus_b, and_1_out, multiplexer_1_out, not_1_out, or_1_out, xor_1_out;
  wire [31:31] multiplexer_2_out;

  Decoder #(.Selector_Bits(4)) decoder_1 (
    .sel(Op), .out_1(SUB), .out_7(SRA));  // open: out_0, out_2, out_3, out_4, out_5, out_6, out_8, out_9, out_10, out_11, out_12, out_13, out_14, out_15
  assign not_1_out = ~B;  // Not not_1, 32 bits wide
  Multiplexer #(.Bits(32)) multiplexer_1 (.sel(SUB), .in_0(B), .in_1(not_1_out), .out(multiplexer_1_out));
  Comparator #(.Bits(32), .Signed("true")) comparator_1 (.a(A), .b(B), .lt(LESS));  // open: gt, eq
  Comparator #(.Bits(32)) comparator_2 (.a(A), .b(B), .eq(EQUAL), .lt(LESS_U));  // open: gt
  Adder32 adder32_1 (.Cin(SUB), .A(A), .B(multiplexer_1_out), .A_plus_B(adder32_1_a_plus_b));  // open: Cout
  assign xor_1_out = A ^ B;  // XOr xor_1, 32 bits wide
  assign or_1_out = A | B;  // Or or_1, 32 bits wide
  assign and_1_out = A & B;  // And and_1, 32 bits wide
  Multiplexer multiplexer_2 (.sel(SRA), .in_0(1'b0), .in_1(A[31]), .out(multiplexer_2_out[31]));
  Multiplexer #(.Bits(32), .Selector_Bits(4)) multiplexer_3 (
    .sel(Op), .in_0(adder32_1_a_plus_b), .in_1(adder32_1_a_plus_b), .in_2(xor_1_out), .in_3(or_1_out),
    .in_4(and_1_out), .in_5({A[30:0], 1'b0}), .in_6({multiplexer_2_out[31], A[31:1]}),
    .in_7({multiplexer_2_out[31], A[31:1]}), .in_8({{31{1'b0}}, LESS}), .in_9({{31{1'b0}}, LESS_U}),
    .in_10({32{1'b0}}), .in_11({32{1'b0}}), .in_12({32{1'b0}}), .in_13({32{1'b0}}), .in_14({32{1'b0}}),
    .in_15({32{1'b0}}), .out(Out));
endmodule
