// Digital circuit Interface test.dig as structural Verilog
module Interface_test (
  input  in_2,
  input  [31:0] in_3,
  input  in_4,
  output [31:0] out_1,
  output [31:0] out_5,
  output out_6,
  output out_7,
  output [31:0] out_8,
  output [31:0] out_9
);

  wire addr, clock, d_ff_1_q, d_ff_2_q, d_ff_3_q, d_ff_4_q, d_ff_5_q, d_ff_6_q, d_ff_7_q, d_ff_8_q, d_ff_9_q,
       demultiplexer_1_out_0, demultiplexer_1_out_1, demultiplexer_2_out_0, demultiplexer_2_out_1, finished,
       ldREG, not_1_out, or_1_out, or_2_out, read_t, STEPS, write_t;
  wire [11:1] interface_1_p6;

  not not_1 (not_1_out, STEPS);
  PullDown pulldown_1 (.out(STEPS));
  PullDown pulldown_2 (.out(write_t));
  PullDown pulldown_3 (.out(read_t));
  PullDown pulldown_4 (.out(addr));
  PullDown pulldown_5 (.out(ldREG));
  D_FF d_ff_1 (.D(not_1_out), .C(clock), .Q(d_ff_1_q));  // open: nQ
  assign out_5 = d_ff_1_q ? 32'ha0 : 32'bz;  // Driver driver_1
  assign addr = d_ff_1_q ? 1'b1 : 1'bz;  // Driver driver_2
  assign STEPS = d_ff_1_q ? 1'b1 : 1'bz;  // Driver driver_3
  or or_1 (or_1_out, d_ff_1_q, demultiplexer_1_out_0);
  D_FF d_ff_2 (.D(or_1_out), .C(clock), .Q(d_ff_2_q));  // open: nQ
  assign read_t = d_ff_2_q ? 1'b1 : 1'bz;  // Driver driver_4
  assign STEPS = d_ff_2_q ? 1'b1 : 1'bz;  // Driver driver_5
  Demultiplexer demultiplexer_1 (
    .sel(finished), .in(d_ff_2_q), .out_0(demultiplexer_1_out_0), .out_1(demultiplexer_1_out_1));
  D_FF d_ff_3 (.D(demultiplexer_1_out_1), .C(~clock), .Q(d_ff_3_q));  // open: nQ
  // Interface interface_1: pin names not known; wires that end beside it: out_5, out_9, in_4, {{9{1'b0}}, addr, read_t, write_t}, clock, {interface_1_p6, finished}, out_5, out_9, out_8, out_6, out_7
  D_FF d_ff_4 (.D(d_ff_3_q), .C(clock), .Q(d_ff_4_q));  // open: nQ
  assign ldREG = d_ff_4_q ? 1'b1 : 1'bz;  // Driver driver_6
  assign STEPS = d_ff_4_q ? 1'b1 : 1'bz;  // Driver driver_7
  D_FF d_ff_5 (.D(d_ff_4_q), .C(clock), .Q(d_ff_5_q));  // open: nQ
  Button button_1 (.out(clock));
  Register #(.Bits(32)) register_1 (.D(out_5), .C(~clock), .en(ldREG), .Q(out_1));
  assign STEPS = d_ff_5_q ? 1'b1 : 1'bz;  // Driver driver_8
  D_FF d_ff_6 (.D(d_ff_5_q), .C(clock), .Q(d_ff_6_q));  // open: nQ
  assign out_5 = d_ff_6_q ? 32'hffb : 32'bz;  // Driver driver_9
  assign addr = d_ff_6_q ? 1'b1 : 1'bz;  // Driver driver_10
  assign STEPS = d_ff_6_q ? 1'b1 : 1'bz;  // Driver driver_11
  or or_2 (or_2_out, d_ff_6_q, demultiplexer_2_out_0);
  D_FF d_ff_7 (.D(or_2_out), .C(clock), .Q(d_ff_7_q));  // open: nQ
  assign out_5 = d_ff_7_q ? 32'habc : 32'bz;  // Driver driver_12
  assign write_t = d_ff_7_q ? 1'b1 : 1'bz;  // Driver driver_13
  Demultiplexer demultiplexer_2 (
    .sel(finished), .in(d_ff_7_q), .out_0(demultiplexer_2_out_0), .out_1(demultiplexer_2_out_1));
  assign STEPS = d_ff_7_q ? 1'b1 : 1'bz;  // Driver driver_14
  D_FF d_ff_8 (.D(demultiplexer_2_out_1), .C(~clock), .Q(d_ff_8_q));  // open: nQ
  assign STEPS = d_ff_8_q ? 1'b1 : 1'bz;  // Driver driver_15
  D_FF d_ff_9 (.D(d_ff_8_q), .C(clock), .Q(d_ff_9_q));  // open: nQ
  assign out_9 = in_2 ? in_3 : 32'bz;  // Driver driver_16
  assign STEPS = d_ff_9_q ? 1'b1 : 1'bz;  // Driver driver_17

  // Other names for the same wires on the sheet: ABUS[31:0] = out_8; DBUS[31:0] = out_9; FC = in_4;
  //   IBUS[31:0] = out_5; READ = out_6; WRITE = out_7

  // Notes on the sheet:
  //   in_3: default 255
  //   Potrebno je da se uhvati signal na falling
  //   egde zato to uslov "finished" se pali na rising edge
endmodule
