// Digital circuit Interface.dig as structural Verilog
module Interface (
  input  [31:0] IBUS_in,
  input  [31:0] DBUS_in,
  input  FC,
  input  [11:0] control_in,
  input  clock,
  output [11:0] control_out,
  output [31:0] IBUS_out,
  output [31:0] DBUS_out,
  output [31:0] ABUS,
  output READ,
  output WRITE
);

  wire and_3_out, and_4_out, d_ff_1_q, d_ff_2_q, d_ff_3_nq, d_ff_4_nq, d_ff_6_q, d_ff_7_nq, MDR_to_IBUS,
       or_1_out, or_2_out, or_3_out, read_finished, read_started, reading, write_finished, write_started,
       writing;
  wire [31:0] MAR_q, MDR_q, multiplexer_1_out;

  D_FF d_ff_1 (.D(control_in[1]), .C(clock), .Q(d_ff_1_q));  // open: nQ
  D_FF d_ff_2 (.D(control_in[0]), .C(clock), .Q(d_ff_2_q));  // open: nQ
  D_FF d_ff_3 (.D(d_ff_1_q), .C(clock), .nQ(d_ff_3_nq));  // open: Q
  D_FF d_ff_4 (.D(d_ff_2_q), .C(clock), .nQ(d_ff_4_nq));  // open: Q
  and and_1 (read_started, d_ff_1_q, d_ff_3_nq);
  and and_2 (write_started, d_ff_2_q, d_ff_4_nq);
  and and_3 (and_3_out, FC, reading);
  and and_4 (and_4_out, FC, writing);
  Multiplexer #(.Bits(32)) multiplexer_1 (.sel(write_started), .in_0(DBUS_in), .in_1(IBUS_in), .out(multiplexer_1_out));
  or or_1 (or_1_out, write_started, read_finished);
  D_FF d_ff_5 (.D(read_finished), .C(clock), .Q(MDR_to_IBUS));  // open: nQ
  or or_2 (or_2_out, and_3_out, and_4_out);
  Register #(.Bits(32)) MDR (.D(multiplexer_1_out), .C(~clock), .en(or_1_out), .Q(MDR_q));
  Register #(.Bits(32)) MAR (.D(IBUS_in), .C(~clock), .en(control_in[2]), .Q(MAR_q));
  RS_FF_AS rs_ff_as_1 (.S(read_started), .R(control_out[0]), .Q(reading));  // open: nQ
  RS_FF_AS rs_ff_as_2 (.S(write_started), .R(control_out[0]), .Q(writing));  // open: nQ
  D_FF d_ff_6 (.D(or_2_out), .C(clock), .Q(d_ff_6_q));  // open: nQ
  or or_3 (or_3_out, writing, reading);
  assign DBUS_out = writing ? MDR_q : 32'bz;  // Driver driver_1
  assign IBUS_out = MDR_to_IBUS ? MDR_q : 32'bz;  // Driver driver_2
  assign ABUS = or_3_out ? MAR_q : 32'bz;  // Driver driver_3
  and and_5 (read_finished, control_out[0], control_in[1]);
  and and_6 (write_finished, control_out[0], control_in[0]);
  D_FF d_ff_7 (.D(d_ff_6_q), .C(clock), .nQ(d_ff_7_nq));  // open: Q
  and and_7 (control_out[0], d_ff_6_q, d_ff_7_nq);
  RS_FF_AS rs_ff_as_3 (.S(read_started), .R(read_finished), .Q(READ));  // open: nQ
  RS_FF_AS rs_ff_as_4 (.S(write_started), .R(write_finished), .Q(WRITE));  // open: nQ

  assign control_out[11:1] = {11{1'b0}};

  // Other names for the same wires on the sheet: write_t = control_in[0]; read_t = control_in[1];
  //   addr = control_in[2]; finished = control_out[0]

  // Notes on the sheet:
  //   IBUS_out: Internal CPU bus
  //   IBUS_in: Internal CPU bus
  //   DBUS_in: Internal CPU bus, default 255
  //   FC: Internal CPU bus
  //   clock: Internal CPU bus
  //   Ovo sluzi da filitrira "finished", tako da se uzima njegova vrednost samo ukoliko je write ili read ukljucen
  //   Delay outputing the read value by one clock cycle
  //   Ovo su signali read i write koji se iskljuce cim 
  //   periferija javi da je zavrsila posao, da ne bi bili 
  //   ukljuceni bezveze i nakon toga
  //   Kada se "finished" signal podigne sa 0 na 1 to
  //   znaci da je periferija (ili memorija) 
  //   primila signal (write/read) uradila sta treba pa 
  //   javlja procesoru da je zavrsila
endmodule
