// Digital circuit mrzime.dig as structural Verilog
module mrzime (
  input  wrR,
  input  [14:0] IR14__0,
  input  [31:0] DIN,
  output [31:0] DOUT1,
  output DOUT2
);

  wire [4:0] IR14__10;
  wire [31:0] D31__0, D31__1, D31__2, D31__3, D31__4, D31__5, D31__6, D31__7, D31__8;
  wire [31:1] demultiplexer_1_out_0, demultiplexer_1_out_1, demultiplexer_1_out_2, demultiplexer_1_out_3,
       demultiplexer_1_out_4, demultiplexer_1_out_5, demultiplexer_1_out_6, demultiplexer_1_out_7,
       demultiplexer_1_out_8, demultiplexer_1_out_9, demultiplexer_1_out_10, demultiplexer_1_out_11,
       demultiplexer_1_out_12, demultiplexer_1_out_13, demultiplexer_1_out_14, demultiplexer_1_out_15,
       demultiplexer_1_out_16, demultiplexer_1_out_17, demultiplexer_1_out_18, demultiplexer_1_out_19,
       demultiplexer_1_out_20, demultiplexer_1_out_21, demultiplexer_1_out_22, demultiplexer_1_out_23,
       demultiplexer_1_out_24, demultiplexer_1_out_25, demultiplexer_1_out_26, demultiplexer_1_out_27,
       demultiplexer_1_out_28, demultiplexer_1_out_29, demultiplexer_1_out_30, demultiplexer_1_out_31;

  Demultiplexer #(.Bits(32), .Selector_Bits(5)) demultiplexer_1 (
    .sel(IR14__10), .in(DIN), .out_0({demultiplexer_1_out_0, D31__0[0]}),
    .out_1({demultiplexer_1_out_1, D31__0[1]}), .out_2({demultiplexer_1_out_2, D31__0[2]}),
    .out_3({demultiplexer_1_out_3, D31__0[3]}), .out_4({demultiplexer_1_out_4, D31__0[4]}),
    .out_5({demultiplexer_1_out_5, D31__0[5]}), .out_6({demultiplexer_1_out_6, D31__0[6]}),
    .out_7({demultiplexer_1_out_7, D31__0[7]}), .out_8({demultiplexer_1_out_8, D31__0[8]}),
    .out_9({demultiplexer_1_out_9, D31__0[9]}), .out_10({demultiplexer_1_out_10, D31__0[10]}),
    .out_11({demultiplexer_1_out_11, D31__0[11]}), .out_12({demultiplexer_1_out_12, D31__0[12]}),
    .out_13({demultiplexer_1_out_13, D31__0[13]}), .out_14({demultiplexer_1_out_14, D31__0[14]}),
    .out_15({demultiplexer_1_out_15, D31__0[15]}), .out_16({demultiplexer_1_out_16, D31__0[16]}),
    .out_17({demultiplexer_1_out_17, D31__0[17]}), .out_18({demultiplexer_1_out_18, D31__0[18]}),
    .out_19({demultiplexer_1_out_19, D31__0[19]}), .out_20({demultiplexer_1_out_20, D31__0[20]}),
    .out_21({demultiplexer_1_out_21, D31__0[21]}), .out_22({demultiplexer_1_out_22, D31__0[22]}),
    .out_23({demultiplexer_1_out_23, D31__0[23]}), .out_24({demultiplexer_1_out_24, D31__0[24]}),
    .out_25({demultiplexer_1_out_25, D31__0[25]}), .out_26({demultiplexer_1_out_26, D31__0[26]}),
    .out_27({demultiplexer_1_out_27, D31__0[27]}), .out_28({demultiplexer_1_out_28, D31__0[28]}),
    .out_29({demultiplexer_1_out_29, D31__0[29]}), .out_30({demultiplexer_1_out_30, D31__0[30]}),
    .out_31({demultiplexer_1_out_31, D31__0[31]}));
  Demultiplexer demultiplexer_2 ();  // open: sel, in, out_0, out_1
  Demultiplexer demultiplexer_3 ();  // open: sel, in, out_0, out_1
  Demultiplexer demultiplexer_4 ();  // open: sel, in, out_0, out_1
  Register #(.Bits(32)) register_1 (.D(D31__1), .en(wrR));  // open: C, Q
  Register #(.Bits(32)) register_2 (.D(D31__2), .en(wrR));  // open: C, Q
  Register #(.Bits(32)) register_3 (.D(D31__3), .en(wrR));  // open: C, Q
  Register #(.Bits(32)) register_4 (.D(D31__4), .en(wrR));  // open: C, Q
  Register #(.Bits(32)) register_5 (.D(D31__5), .en(wrR));  // open: C, Q
  Register #(.Bits(32)) register_6 (.D(D31__6), .en(wrR));  // open: C, Q
  Register #(.Bits(32)) register_7 (.D(D31__7), .en(wrR));  // open: C, Q
  Register #(.Bits(32)) register_8 (.D(D31__8), .en(wrR));  // open: C, Q
  Register #(.Bits(32)) register_9 (.D(D31__1), .en(wrR));  // open: C, Q
  Register #(.Bits(32)) register_10 (.D(D31__2), .en(wrR));  // open: C, Q
  Register #(.Bits(32)) register_11 (.D(D31__3), .en(wrR));  // open: C, Q
  Register #(.Bits(32)) register_12 (.D(D31__4), .en(wrR));  // open: C, Q
  Register #(.Bits(32)) register_13 (.D(D31__5), .en(wrR));  // open: C, Q
  Register #(.Bits(32)) register_14 (.D(D31__6), .en(wrR));  // open: C, Q
  Register #(.Bits(32)) register_15 (.D(D31__7), .en(wrR));  // open: C, Q
  Register #(.Bits(32)) register_16 (.D(D31__8), .en(wrR));  // open: C, Q
  Register #(.Bits(32)) register_17 (.D(D31__1), .en(wrR));  // open: C, Q
  Register #(.Bits(32)) register_18 (.D(D31__2), .en(wrR));  // open: C, Q
  Register #(.Bits(32)) register_19 (.D(D31__3), .en(wrR));  // open: C, Q
  Register #(.Bits(32)) register_20 (.D(D31__4), .en(wrR));  // open: C, Q
  Register #(.Bits(32)) register_21 (.D(D31__5), .en(wrR));  // open: C, Q
  Register #(.Bits(32)) register_22 (.D(D31__6), .en(wrR));  // open: C, Q
  Register #(.Bits(32)) register_23 (.D(D31__7), .en(wrR));  // open: C, Q
  Register #(.Bits(32)) register_24 (.D(D31__8), .en(wrR));  // open: C, Q
  Register #(.Bits(32)) register_25 (.D(D31__1), .en(wrR));  // open: C, Q
  Register #(.Bits(32)) register_26 (.D(D31__2), .en(wrR));  // open: C, Q
  Register #(.Bits(32)) register_27 (.D(D31__3), .en(wrR));  // open: C, Q
  Register #(.Bits(32)) register_28 (.D(D31__4), .en(wrR));  // open: C, Q
  Register #(.Bits(32)) register_29 (.D(D31__5), .en(wrR));  // open: C, Q
  Register #(.Bits(32)) register_30 (.D(D31__6), .en(wrR));  // open: C, Q
  Register #(.Bits(32)) register_31 (.D(D31__7), .en(wrR));  // open: C, Q
  Register #(.Bits(32)) register_32 (.D(D31__8), .en(wrR));  // open: C, Q
  // Pins of 1 and 32 bits meet at {demultiplexer_1_out_0, D31__0[0]}
  // Pins of 1 and 32 bits meet at {demultiplexer_1_out_1, D31__0[1]}
  // Pins of 1 and 32 bits meet at {demultiplexer_1_out_2, D31__0[2]}
  // Pins of 1 and 32 bits meet at {demultiplexer_1_out_3, D31__0[3]}
  // Pins of 1 and 32 bits meet at {demultiplexer_1_out_4, D31__0[4]}
  // Pins of 1 and 32 bits meet at {demultiplexer_1_out_5, D31__0[5]}
  // Pins of 1 and 32 bits meet at {demultiplexer_1_out_6, D31__0[6]}
  // Pins of 1 and 32 bits meet at {demultiplexer_1_out_7, D31__0[7]}
  // Pins of 1 and 32 bits meet at {demultiplexer_1_out_8, D31__0[8]}
  // Pins of 1 and 32 bits meet at {demultiplexer_1_out_9, D31__0[9]}
  // Pins of 1 and 32 bits meet at {demultiplexer_1_out_10, D31__0[10]}
  // Pins of 1 and 32 bits meet at {demultiplexer_1_out_11, D31__0[11]}

  // Other names for the same wires on the sheet: wr = wrR
endmodule
